# Fritzing sketch lomba (saved by Fritzing 0.9.3b)
breadboards: 1

parts:
  BATT1 = LiPoly Battery (1300mAh)
  ESP32_DEV_KIT1 = MH-ET LIVE ESP32 DEVKIT 38 pins
  LORA_SX1279 = Osoyoo SX1278-ra-02
  OLED_I2C1 = OLED 128x64 I2C Monochrome Display

nets:
  3V3: BATT1.positive, ESP32_DEV_KIT1.3V3, ESP32_DEV_KIT1.RST, LORA_SX1279.3.3V, OLED_I2C1.VDD
  GND: BATT1.negative, ESP32_DEV_KIT1.GND, LORA_SX1279.GND, OLED_I2C1.GND
  N1: ESP32_DEV_KIT1.IO14, LORA_SX1279.RST
  N2: ESP32_DEV_KIT1.IO23, LORA_SX1279.MOSI
  N3: ESP32_DEV_KIT1.IO22, ESP32_DEV_KIT1.TXD0, OLED_I2C1.SCK
  N4: ESP32_DEV_KIT1.IO21, OLED_I2C1.SDA
  N5: ESP32_DEV_KIT1.IO19, LORA_SX1279.MISO
  N6: ESP32_DEV_KIT1.IO18, LORA_SX1279.SCK
  N7: ESP32_DEV_KIT1.IO5, ESP32_DEV_KIT1.IO17, LORA_SX1279.NSS

custom parts:
  LiPoly Battery (1300mAh): Lithium Ion Polymer Battery (1300mAh)
  MH-ET LIVE ESP32 DEVKIT 38 pins: http://mh.nodebb.com/topic/2/mh-et-live-esp32-devkit
  Osoyoo SX1278-ra-02: Osoyoo Long Distance wireless transceiver Uart LoRa Module.
